# Fritzing sketch Fritzing Sketch (saved by Fritzing 1.0.0rc)
breadboards: 1

parts:
  Mosfet_Relay = DIP - 18 pins [chip_label=IC package="DIP (Dual Inline) [THT]"]
  ESP32_DevKit = DIP - 38 pins [chip_label=IC package="DIP (Dual Inline) [THT]"]
  Ball_Release_Valve = SIP - 2 pins [chip_label=IC package="SIP (Single Inline) [THT]"]
  Bleed_Valve = SIP - 2 pins [chip_label=IC package="SIP (Single Inline) [THT]"]
  Charge_Valve = SIP - 2 pins [chip_label=IC package="SIP (Single Inline) [THT]"]
  Pin_Release_Valve = SIP - 2 pins [chip_label=IC package="SIP (Single Inline) [THT]"]
  Wiper_Sensor = SIP - 2 pins [chip_label=IC package="SIP (Single Inline) [THT]"]
  Ball_Sensor = SIP - 2 pins [chip_label=IC package="SIP (Single Inline) [THT]"]
  Pin_Sensor = SIP - 2 pins [chip_label=IC package="SIP (Single Inline) [THT]"]
  Backside_Pressure_Transducer = SIP - 3 pins [chip_label=IC package="SIP (Single Inline) [THT]"]
  Bottle_Pressure_Transducer = SIP - 3 pins [chip_label=IC package="SIP (Single Inline) [THT]"]
  12V_Battery = SIP - 2 pins [chip_label=IC package="SIP (Single Inline) [THT]"]
  R1 = Resistor [tolerance=±5% resistance=220 package="2010 [SMD]"]
  R2 = Resistor [tolerance=±5% resistance=330 package="2010 [SMD]"]
  R3 = Resistor [tolerance=±5% resistance=220 package="2010 [SMD]"]
  R4 = Resistor [tolerance=±5% resistance=330 package="2010 [SMD]"]
  Pin_21_=_100% = Basic FET P-Channel [package="TO220 [THT]"]  # not connected
  Pin_19_=_80% = LM35 Temperature Sensor [package="TO92 [THT]"]  # not connected
  Pin_17_=_40% = LM35 Temperature Sensor [package="TO92 [THT]"]  # not connected
  Pin_16_=_20% = LM35 Temperature Sensor [package="TO92 [THT]"]  # not connected
  Pin_18_=_60% = LM35 Temperature Sensor [package="TO92 [THT]"]  # not connected

nets:
  N1: Mosfet_Relay.pin1, Backside_Pressure_Transducer.pin1, Bottle_Pressure_Transducer.pin1, 12V_Battery.pin1
  N2: Mosfet_Relay.pin2, Backside_Pressure_Transducer.pin2, Bottle_Pressure_Transducer.pin2, 12V_Battery.pin2
  N3: Mosfet_Relay.pin3, Charge_Valve.pin2
  N4: Mosfet_Relay.pin4, Charge_Valve.pin1
  N5: Mosfet_Relay.pin5, Bleed_Valve.pin2
  N6: Mosfet_Relay.pin6, Bleed_Valve.pin1
  N7: Mosfet_Relay.pin7, Pin_Release_Valve.pin2
  N8: Mosfet_Relay.pin8, Pin_Release_Valve.pin1
  N9: Mosfet_Relay.pin9, Ball_Release_Valve.pin2
  N10: Mosfet_Relay.pin10, Ball_Release_Valve.pin1
  N11: Mosfet_Relay.pin11, ESP32_DevKit.pin10
  N12: Mosfet_Relay.pin12, Mosfet_Relay.pin14, Mosfet_Relay.pin16, Mosfet_Relay.pin18, ESP32_DevKit.pin18, Wiper_Sensor.pin2, Ball_Sensor.pin2, Pin_Sensor.pin2, R2.Pin_1, R4.Pin_1
  N13: Mosfet_Relay.pin13, ESP32_DevKit.pin11
  N14: Mosfet_Relay.pin15, ESP32_DevKit.pin12
  N15: Mosfet_Relay.pin17, ESP32_DevKit.pin13
  N16: ESP32_DevKit.pin5, R3.Pin_1, R4.Pin_0
  N17: ESP32_DevKit.pin6, R1.Pin_1, R2.Pin_0
  N18: ESP32_DevKit.pin7, Pin_Sensor.pin1
  N19: ESP32_DevKit.pin8, Ball_Sensor.pin1
  N20: ESP32_DevKit.pin9, Wiper_Sensor.pin1
  N21: Backside_Pressure_Transducer.pin3, R3.Pin_0
  N22: Bottle_Pressure_Transducer.pin3, R1.Pin_0

custom parts:
  DIP - 18 pins: A DIP stand-in part for whatever IC you want. With 18 pins on a 300mil dual inline package (DIP) footprint.
  DIP - 38 pins: A DIP stand-in part for whatever IC you want. With 38 pins on a 300mil dual inline package (DIP) footprint.
  SIP - 2 pins: A SIP stand-in part for whatever you want. With 2 pins on a 300 mil single inline package (SIP) footprint.
  SIP - 2 pins: A SIP stand-in part for whatever you want. With 2 pins on a 300 mil single inline package (SIP) footprint.
  SIP - 3 pins: A SIP stand-in part for whatever you want. With 3 pins on a 300 mil single inline package (SIP) footprint.
  SIP - 2 pins: A SIP stand-in part for whatever you want. With 2 pins on a 300 mil single inline package (SIP) footprint.
